# Fritzing sketch SlackLight2 (saved by Fritzing 0.9.3b)
circuit board: 5.99999cm x 5.99999cm
breadboards: 1

parts:
  Part1 = ws2812b [package="smd 2812b"]
  Part2 = ws2812b [package="smd 2812b"]
  Part3 = ws2812b [package="smd 2812b"]
  Part5 = ws2812b [package="smd 2812b"]
  Part6 = ws2812b [package="smd 2812b"]
  Part7 = ws2812b [package="smd 2812b"]
  Part8 = ws2812b [package="smd 2812b"]
  J3 = female pin header, 2 pins [form="♀ (female)"]
  J1 = female alternating pin header, 8 pins [form="♀ (female)"]  # not connected
  J2 = female alternating pin header, 8 pins [form="♀ (female)"]
  Part4 = ws2812b [package="smd 2812b"]

nets:
  5V: Part1.VDD, Part2.VDD, Part3.VDD, Part5.VDD, Part6.VDD, Part7.VDD, Part8.VDD, J3.pin1, J2.pin8, Part4.VDD
  N1: Part1.DOUT, Part8.DIN
  GND: Part1.VSS, Part2.VSS, Part3.VSS, Part5.VSS, Part6.VSS, Part7.VSS, Part8.VSS, J3.pin2, J2.pin7, Part4.VSS
  N2: Part1.DIN, J2.pin2
  N3: Part2.DIN, Part3.DOUT
  N4: Part3.DIN, Part4.DOUT
  N5: Part5.DOUT, Part4.DIN
  N6: Part5.DIN, Part6.DOUT
  N7: Part6.DIN, Part7.DOUT
  N8: Part7.DIN, Part8.DOUT

notes:
  5V  GND
  GND  5V
  SlackLight v2
  caseyfulton.com
